# Fritzing sketch circuit design v1.0 (saved by Fritzing 0.9.3b)

parts:
  VCC1_-_6xAA_Cells = Battery block 9V
  S1_-_Power_Switch = SPST Switch [package=switch-spdt_lock.007s]
  Water_Sensor = Soil Moisture Sensor [part_number="Capacative Soil Moisture Sensor v1.2"]
  LED1 = LED - 5mm [color="Green (565nm)" package="5 mm [THT]"]
  Water_Pump = DC Motor
  M2_-_Buck_Converter = RioRand LM2596
  D1 = Rectifier Diode [part_number=1N4001 package="300 mil [THT]"]
  R1 = Resistor [tolerance=±5% resistance=150 package=THT]
  Q2 = NPN-Transistor [part_number=BC548 package="TO92 [THT]"]
  Relay = DS2Y-5-DC5V [part_number=DS2Y-5-DC5V]
  WeMos_D1_R2 = WeMos D1 R2
  R2 = Resistor [tolerance=±5% resistance=100k package=THT]
  R3 = Resistor [tolerance=±5% resistance=68k package=THT]
  R4 = Resistor [tolerance=±5% resistance=330 package=THT]

nets:
  N1: VCC1_-_6xAA_Cells.-, M2_-_Buck_Converter.Pin_2
  N2: VCC1_-_6xAA_Cells.+, S1_-_Power_Switch.P, R2.Pin_0
  N3: S1_-_Power_Switch.S, M2_-_Buck_Converter.Pin_1
  VCC: Water_Sensor.VCC, Relay.1_+, WeMos_D1_R2.3.3V
  N4: Water_Sensor.GND, Q2.C
  N5: Water_Sensor.SIG, WeMos_D1_R2.A0
  N6: LED1.cathode, R1.Pin_0
  N7: LED1.anode, WeMos_D1_R2.(D7)
  N8: Water_Pump.pin_1, D1.cathode, Relay.9_N.O.
  GND: Water_Pump.pin_2, M2_-_Buck_Converter.Pin_4, D1.anode, R1.Pin_1, Q2.E, Relay.16_-, WeMos_D1_R2.GND, R3.Pin_1
  N9: M2_-_Buck_Converter.Pin_3, Relay.4_COM, WeMos_D1_R2.VIN
  N10: Q2.B, WeMos_D1_R2.D4
  N11: WeMos_D1_R2.D0/RX, R4.Pin_0
  N12: WeMos_D1_R2.D2, R2.Pin_1, R3.Pin_0
  N13: WeMos_D1_R2.RESET, R4.Pin_1

custom parts:
  WeMos D1 R2: The D1 R2 is a mini wifi board based on the ESP-8266EX.
